// Logisim project ejemplo02.circ as structural Verilog: 1 circuit, main circuit main
module main (
  input  dir
);

  wire clk, d11, d11a, d11b, d12, d12a, d12b, d21, d21a, d21b, d22, d22a, d22b, d_ff_1_q, g11_out, or_1_out,
       or_2_out, or_3_out;
  wire [1:0] d_ff_2_q;

  Clock clock_1 (.out(clk));
  or g11 (g11_out, d11a, d11b);
  or or_1 (or_1_out, d21a, d21b);
  D_Flip_Flop u_d11 (.clk(clk), .D(g11_out), .Q(d11));  // open: Qn, preset, en, reset
  Demultiplexer #(.disabled(0), .enable("false")) demultiplexer_1 (.out0(d12a), .out1(d22a), .in(d11), .sel(dir));
  Demultiplexer #(.disabled(0), .enable("false")) demultiplexer_2 (.out0(d22b), .out1(d12b), .in(d21), .sel(dir));
  D_Flip_Flop u_d21 (.clk(clk), .D(or_1_out), .Q(d21));  // open: Qn, preset, en, reset
  D_Flip_Flop d_ff_1 (.clk(clk), .D(d_ff_2_q[0]), .Q(d_ff_1_q));  // open: Qn, preset, en, reset
  D_Flip_Flop d_ff_2 (.clk(clk), .D(d_ff_1_q), .Q(d_ff_2_q[0]));  // open: Qn, preset, en, reset
  DotMatrix #(.matrixcols(2), .matrixrows(2)) dotmatrix_1 (.col0({d11, d21}), .col1({d12, d22}));
  DotMatrix #(.matrixcols(2), .matrixrows(2)) dotmatrix_2 (.col1(d_ff_2_q));  // open: col0
  not not_1 (d_ff_2_q[1], d_ff_2_q[0]);
  D_Flip_Flop u_d12 (.clk(clk), .D(or_2_out), .Q(d12));  // open: Qn, preset, en, reset
  or or_2 (or_2_out, d12a, d12b);
  D_Flip_Flop u_d22 (.clk(clk), .D(or_3_out), .Q(d22));  // open: Qn, preset, en, reset
  or or_3 (or_3_out, d22a, d22b);
  Demultiplexer #(.disabled(0), .enable("false")) demultiplexer_3 (.out0(d11a), .out1(d21a), .in(d12), .sel(dir));
  Demultiplexer #(.disabled(0), .enable("false")) demultiplexer_4 (.out0(d21b), .out1(d11b), .in(d22), .sel(dir));
endmodule
