// Logisim project proyectoFinal.circ as structural Verilog: 1 circuit, main circuit main
module main (
  input  in_1,
  input  in_2,
  input  in_3,
  input  in_4,
  input  in_5,
  input  in_6,
  input  in_7,
  input  in_8,
  input  in_9,
  input  in_10,
  input  in_11,
  input  in_12,
  input  in_13,
  input  in_14,
  input  in_15,
  input  in_16,
  input  in_17,
  input  in_18,
  input  SALTO,
  input  in_20,
  input  in_21,
  input  in_22,
  input  in_23,
  input  in_24,
  input  in_25,
  input  in_26,
  input  in_27,
  input  in_28,
  input  in_29,
  input  in_30,
  input  in_31,
  input  in_32,
  input  in_33,
  input  in_34,
  input  in_35,
  input  in_36,
  input  in_37,
  input  in_38,
  input  in_39,
  input  in_40,
  input  in_41,
  input  in_42,
  input  in_43,
  input  in_44,
  input  in_45,
  input  in_46,
  input  in_47,
  input  in_48,
  input  in_49,
  input  in_50,
  input  in_51,
  input  in_52,
  input  in_53
);

  wire _30f1, _30f2, _30f3, _30f4, _30f5, _30f6, _30f7, _30f8, _30f9, _30f10, _30f11, _30f12, _30f13, _30f14,
       _31f1, _31f2, _31f3, _31f4, _31f5, _31f6, _31f7, _31f8, _31f9, _31f10, _31f11, _31f12, _31f13, _31f14,
       A, a1, a1a, a2, a2a, a2b, a3, a3a, a3b, a4, a4a, a4b, a5a, a5b, a_t, and_1_out, and_4_out, and_7_out,
       and_8_out, and_9_out, and_10_out, and_11_out, and_12_out, and_13_out, and_14_out, and_15_out,
       and_16_out, and_17_out, and_18_out, and_19_out, and_20_out, and_21_out, and_22_out, and_23_out,
       and_24_out, and_25_out, and_26_out, and_27_out, and_28_out, and_29_out, and_30_out, and_31_out,
       and_32_out, and_33_out, and_34_out, and_35_out, and_36_out, and_37_out, and_38_out, and_39_out,
       and_40_out, and_41_out, and_42_out, and_43_out, and_44_out, and_45_out, and_46_out, and_47_out,
       and_48_out, and_49_out, and_50_out, and_51_out, and_52_out, and_53_out, and_54_out, and_55_out,
       and_56_out, and_57_out, and_58_out, and_59_out, and_60_out, and_61_out, and_62_out, and_63_out,
       and_64_out, and_65_out, and_66_out, and_67_out, ap1, ap2, ap3, ap4, clock_1_out, d, d1a, d2a, d2b,
       d3a, d3b, d4a, d4b, d5a, d5b, d6a, d6b, d7a, d7b, d8a, d8b, d22a, dir, dirs, e, e1, e1fp, e1fs, e2,
       e2fp, e2fs, e3, e3fp, e3fs, e4, e4fp, e4fs, e5, e5fp, e5fs, e6, e6fp, e6fs, e7, e7fp, e7fs, e8, e8fp,
       e8fs, e9, e9fp, e9fs, e10, e10fp, e10fs, e11, e11fp, e11fs, e12, e12fp, e12fs, e13, e13fp, e13fs, e14,
       e14fp, e14fs, e15, e15fp, e15fs, e16, e16fp, e16fs, e17, e17fp, e17fs, e18, e18fp, e18fs, e19, e19fp,
       e19fs, e20, e20fp, e20fs, e21, e21fp, e21fs, e22, e22fp, e22fs, e23, e23fp, e23fs, e24, e24fp, e24fs,
       e25, e25fp, e25fs, e26, e26fp, e26fs, e27, e27fp, e27fs, e28, e28fp, e28fs, e29, e29fp, e29fs, e30,
       e30fp, e30fs, e31, e31fp, e31fs, e32, e32fp, e32fs, f, ffp4, ffp5, ffp6, ffp7, fp4, fp5, fp6, fp7,
       multiplexer_19_out, multiplexer_20_out, multiplexer_21_out, multiplexer_22_out, multiplexer_23_out,
       multiplexer_24_out, multiplexer_25_out, multiplexer_26_out, multiplexer_27_out, multiplexer_28_out,
       multiplexer_29_out, multiplexer_30_out, multiplexer_31_out, multiplexer_32_out, multiplexer_33_out,
       multiplexer_34_out, multiplexer_35_out, multiplexer_36_out, multiplexer_37_out, multiplexer_38_out,
       multiplexer_39_out, multiplexer_40_out, multiplexer_41_out, multiplexer_42_out, multiplexer_43_out,
       multiplexer_44_out, multiplexer_45_out, multiplexer_46_out, multiplexer_47_out, multiplexer_48_out,
       multiplexer_49_out, multiplexer_50_out, neg, NO, not_1_out, not_2_out, not_3_out, not_4_out,
       not_5_out, not_6_out, not_7_out, not_9_out, not_10_out, not_11_out, not_14_out, not_15_out, obj, op,
       op1, or_30_out, or_31_out, or_32_out, or_33_out, or_34_out, or_35_out, or_36_out, or_37_out,
       or_38_out, or_39_out, or_40_out, or_41_out, or_42_out, pr, prn, rj, rt, s, s1, s2, s3, s4, s5, s6, s7,
       sa, so1, so2, so3, so4, so5, so6, so7, sp1, sp2, sp3, sp4, sp5, sp6, sp7, undriven;
  wire [6:0] keyboard_1_data;

  DotMatrix #(.inputtype("row"), .matrixcols(32), .matrixrows(16)) dotmatrix_1 (
    .row0({e32fs, e31fs, e30fs, e29fs, e28fs, e27fs, e26fs, e25fs, e24fs, e23fs, e22fs, e21fs, e20fs, e19fs, e18fs, e17fs, e16fs, e15fs, e14fs, e13fs, e12fs, e11fs, e10fs, e9fs, e8fs, e7fs, e6fs, e5fs, e4fs, e3fs, e2fs, e1fs}),
    .row1({e32fs, e31fs, e30fs, e29fs, e28fs, e27fs, e26fs, e25fs, e24fs, e23fs, e22fs, e21fs, e20fs, e19fs, e18fs, e17fs, e16fs, e15fs, e14fs, e13fs, e12fs, e11fs, e10fs, e9fs, e8fs, e7fs, e6fs, e5fs, e4fs, e3fs, e2fs, e1fs}),
    .row2({e32fs, _31f14, _30f14, e29fs, e28fs, e27fs, e26fs, e25fs, e24fs, e23fs, e22fs, e21fs, e20fs, e19fs, e18fs, e17fs, e16fs, e15fs, e14fs, e13fs, e12fs, e11fs, e10fs, e9fs, e8fs, e7fs, e6fs, e5fs, e4fs, e3fs, e2fs, e1fs}),
    .row3({e32fs, _31f13, _30f13, e29fs, e28fs, e27fs, e26fs, e25fs, e24fs, e23fs, e22fs, e21fs, e20fs, e19fs, e18fs, e17fs, e16fs, e15fs, e14fs, e13fs, e12fs, e11fs, e10fs, e9fs, e8fs, e7fs, e6fs, e5fs, e4fs, e3fs, e2fs, e1fs}),
    .row4({e32fs, _31f12, _30f12, e29fs, e28fs, e27fs, e26fs, e25fs, e24fs, e23fs, e22fs, e21fs, e20fs, e19fs, e18fs, e17fs, e16fs, e15fs, e14fs, e13fs, e12fs, e11fs, e10fs, e9fs, e8fs, e7fs, e6fs, e5fs, e4fs, e3fs, e2fs, e1fs}),
    .row5({e32fs, _31f11, _30f11, e29fs, e28fs, e27fs, e26fs, e25fs, e24fs, e23fs, e22fs, e21fs, e20fs, e19fs, e18fs, e17fs, e16fs, e15fs, e14fs, e13fs, e12fs, e11fs, e10fs, e9fs, e8fs, e7fs, e6fs, e5fs, e4fs, e3fs, e2fs, e1fs}),
    .row6({e32fs, _31f10, _30f10, e29fs, e28fs, e27fs, e26fs, e25fs, e24fs, e23fs, e22fs, e21fs, e20fs, e19fs, e18fs, e17fs, e16fs, e15fs, e14fs, e13fs, e12fs, e11fs, e10fs, e9fs, e8fs, e7fs, e6fs, e5fs, e4fs, e3fs, e2fs, e1fs}),
    .row7({e32fs, _31f9, _30f9, e29fs, e28fs, e27fs, e26fs, e25fs, e24fs, e23fs, e22fs, e21fs, e20fs, e19fs, e18fs, e17fs, e16fs, e15fs, e14fs, e13fs, e12fs, e11fs, e10fs, e9fs, e8fs, e7fs, e6fs, e5fs, e4fs, e3fs, e2fs, e1fs}),
    .row8({e32fs, _31f8, _30f8, e29fs, e28fs, e27fs, e26fs, e25fs, e24fs, e23fs, e22fs, e21fs, e20fs, e19fs, e18fs, e17fs, e16fs, e15fs, e14fs, e13fs, e12fs, e11fs, e10fs, e9fs, e8fs, e7fs, e6fs, e5fs, e4fs, e3fs, e2fs, e1fs}),
    .row9({e32fs, _31f7, _30f7, e29fs, e28fs, e27fs, e26fs, e25fs, e24fs, e23fs, e22fs, e21fs, e20fs, e19fs, e18fs, e17fs, e16fs, e15fs, e14fs, e13fs, e12fs, e11fs, e10fs, e9fs, e8fs, e7fs, e6fs, e5fs, e4fs, e3fs, e2fs, e1fs}),
    .row10({in_3, _31f6, _30f6, {29{in_1}}}),
    .row11({e32fp, _31f5, _30f5, e29fp, e28fp, e27fp, e26fp, e25fp, e24fp, e23fp, e22fp, e21fp, e20fp, e19fp, e18fp, e17fp, e16fp, e15fp, e14fp, e13fp, e12fp, e11fp, e10fp, e9fp, e8fp, e7fp, e6fp, e5fp, e4fp, e3fp, e2fp, e1fp}),
    .row12({e32fp, _31f4, _30f4, e29fp, e28fp, e27fp, e26fp, e25fp, e24fp, e23fp, e22fp, e21fp, e20fp, e19fp, e18fp, e17fp, e16fp, e15fp, e14fp, e13fp, e12fp, e11fp, e10fp, e9fp, e8fp, e7fp, e6fp, e5fp, e4fp, e3fp, e2fp, e1fp}),
    .row13({e32fp, _31f3, _30f3, e29fp, e28fp, e27fp, e26fp, e25fp, e24fp, e23fp, e22fp, e21fp, e20fp, e19fp, e18fp, e17fp, e16fp, e15fp, e14fp, e13fp, e12fp, e11fp, e10fp, e9fp, e8fp, e7fp, e6fp, e5fp, e4fp, e3fp, e2fp, e1fp}),
    .row14({e32fp, _31f2, _30f2, e29fp, e28fp, e27fp, e26fp, e25fp, e24fp, e23fp, e22fp, e21fp, e20fp, e19fp, e18fp, e17fp, e16fp, e15fp, e14fp, e13fp, e12fp, e11fp, e10fp, e9fp, e8fp, e7fp, e6fp, e5fp, e4fp, e3fp, e2fp, e1fp}),
    .row15({e32fp, _31f1, _30f1, e29fp, e28fp, e27fp, e26fp, e25fp, e24fp, e23fp, e22fp, e21fp, e20fp, e19fp, e18fp, e17fp, e16fp, e15fp, e14fp, e13fp, e12fp, e11fp, e10fp, e9fp, e8fp, e7fp, e6fp, e5fp, e4fp, e3fp, e2fp, e1fp}));
  Keyboard keyboard_1 (.clk(rj), .data(keyboard_1_data));  // open: re, clr, avail
  not not_1 (not_1_out, s1);
  not not_2 (not_2_out, s5);
  Multiplexer #(.enable("false")) multiplexer_1 (.in0(in_6), .in1(neg), .out(sp1), .sel(not_1_out));
  Multiplexer #(.enable("false")) multiplexer_2 (.in0(in_17), .in1(neg), .out(sp5), .sel(not_2_out));
  or or_1 (_31f1, sp1, e31fp);
  or or_2 (_31f2, sp2, e31fp);
  or or_3 (_30f1, sp1, e30fp);
  or or_4 (_30f2, sp2, e30fp);
  Multiplexer #(.enable("false")) multiplexer_3 (.in0(1'b0), .in1(1'b1), .out(ap1), .sel(a1));
  Multiplexer #(.enable("false")) multiplexer_4 (.in0(1'b0), .in1(1'b1), .out(ap2), .sel(a2));
  D_Flip_Flop d_ff_1 (.clk(rj), .D(e32), .Q(e1), .preset(obj), .en(NO), .reset(rt));  // open: Qn
  D_Flip_Flop d_ff_2 (.clk(rj), .D(e8), .Q(e9), .reset(rt));  // open: Qn, preset, en
  D_Flip_Flop d_ff_3 (.clk(rj), .D(e16), .Q(e17), .reset(rt));  // open: Qn, preset, en
  D_Flip_Flop d_ff_4 (.clk(rj), .D(e24), .Q(e25), .reset(rt));  // open: Qn, preset, en
  or or_5 (obj, pr, and_1_out);
  and and_1 (and_1_out, e20, e21);
  Multiplexer #(.enable("false")) multiplexer_5 (.in0(in_8), .in1(neg), .out(so1), .sel(s1));
  not not_3 (not_3_out, s2);
  Multiplexer #(.enable("false")) multiplexer_6 (.in0(SALTO), .in1(neg), .out(so5), .sel(s5));
  not not_4 (not_4_out, s6);
  or or_6 (_31f3, sp3, e31fp);
  or or_7 (_31f4, ffp4, e31fp);
  or or_8 (_31f5, ffp5, e31fp);
  or or_9 (_30f3, sp3, e30fp);
  or or_10 (_30f4, ffp4, e30fp);
  or or_11 (_30f5, ffp5, e30fp);
  nand nand_1 (fp7, ap1, sp7);
  nand nand_2 (fp6, ap2, sp6);
  D_Flip_Flop d_ff_5 (.clk(rj), .D(e1), .Q(e2), .preset(obj), .en(NO), .reset(rt));  // open: Qn
  D_Flip_Flop d_ff_6 (.clk(rj), .D(e9), .Q(e10), .reset(rt));  // open: Qn, preset, en
  D_Flip_Flop d_ff_7 (.clk(rj), .D(e17), .Q(e18), .reset(rt));  // open: Qn, preset, en
  D_Flip_Flop d_ff_8 (.clk(rj), .D(e25), .Q(e26), .reset(rt));  // open: Qn, preset, en
  Multiplexer #(.enable("false")) multiplexer_7 (.in0(in_7), .in1(neg), .out(sp2), .sel(not_3_out));
  Multiplexer #(.enable("false")) multiplexer_8 (.in0(in_18), .in1(neg), .out(sp6), .sel(not_4_out));
  or or_12 (_31f6, ffp6, in_26);
  or or_13 (_31f7, ffp7, e31fs);
  or or_14 (_31f8, so1, e31fs);
  or or_15 (_30f6, ffp6, in_30);
  or or_16 (_30f7, ffp7, e30fs);
  or or_17 (_30f8, so1, e30fs);
  and and_2 (ffp7, sp7, fp7);
  and and_3 (ffp6, sp6, fp6);
  D_Flip_Flop d_ff_9 (.clk(rj), .D(e2), .Q(e3), .en(prn), .reset(rt));  // open: Qn, preset
  D_Flip_Flop d_ff_10 (.clk(rj), .D(e10), .Q(e11), .reset(rt));  // open: Qn, preset, en
  D_Flip_Flop d_ff_11 (.clk(rj), .D(e18), .Q(e19), .reset(rt));  // open: Qn, preset, en
  D_Flip_Flop d_ff_12 (.clk(rj), .D(e26), .Q(e27), .reset(rt));  // open: Qn, preset, en
  Comparator #(.width(7)) comparator_1 (.a(keyboard_1_data), .b(7'b1110111), .eq(d));  // open: gt, lt
  Comparator #(.width(7)) comparator_2 (.a(keyboard_1_data), .b(7'b1111001), .eq(a_t));  // open: gt, lt
  Comparator #(.width(7)) comparator_3 (.a(keyboard_1_data), .b(7'b1110110), .eq(pr));  // open: gt, lt
  Multiplexer #(.enable("false")) multiplexer_9 (.in0(in_9), .in1(neg), .out(so2), .sel(s2));
  not not_5 (not_5_out, s3);
  Multiplexer #(.enable("false")) multiplexer_10 (.in0(in_20), .in1(neg), .out(so6), .sel(s6));
  not not_6 (not_6_out, s7);
  or or_18 (_31f9, so2, e31fs);
  or or_19 (_31f10, so3, e31fs);
  or or_20 (_31f11, so4, e31fs);
  or or_21 (_30f9, so2, e30fs);
  or or_22 (_30f10, so3, e30fs);
  or or_23 (_30f11, so4, e30fs);
  D_Flip_Flop d_ff_13 (.clk(rj), .D(e3), .Q(e4), .reset(rt));  // open: Qn, preset, en
  D_Flip_Flop d_ff_14 (.clk(rj), .D(e11), .Q(e12), .reset(rt));  // open: Qn, preset, en
  D_Flip_Flop d_ff_15 (.clk(rj), .D(e19), .Q(e20), .reset(rt));  // open: Qn, preset, en
  D_Flip_Flop d_ff_16 (.clk(rj), .D(e27), .Q(e28), .reset(rt));  // open: Qn, preset, en
  Button button_1 (.out(rt));
  Multiplexer #(.enable("false")) multiplexer_11 (.in0(in_10), .in1(neg), .out(sp3), .sel(not_5_out));
  Multiplexer #(.enable("false")) multiplexer_12 (.in0(in_21), .in1(neg), .out(sp7), .sel(not_6_out));
  or or_24 (_31f12, so5, e31fs);
  or or_25 (_31f13, so6, e31fs);
  or or_26 (_31f14, so7, e31fs);
  or or_27 (_30f12, so5, e30fs);
  or or_28 (_30f13, so6, e30fs);
  or or_29 (_30f14, so7, e30fs);
  Multiplexer #(.enable("false")) multiplexer_13 (.in0(1'b0), .in1(1'b1), .out(ap3), .sel(a3));
  Multiplexer #(.enable("false")) multiplexer_14 (.in0(1'b0), .in1(1'b1), .out(ap4), .sel(a4));
  D_Flip_Flop d_ff_17 (.clk(rj), .D(e4), .Q(e5), .reset(rt));  // open: Qn, preset, en
  D_Flip_Flop d_ff_18 (.clk(rj), .D(e12), .Q(e13), .reset(rt));  // open: Qn, preset, en
  D_Flip_Flop d_ff_19 (.clk(rj), .D(e20), .Q(e21), .reset(rt));  // open: Qn, preset, en
  D_Flip_Flop d_ff_20 (.clk(rj), .D(e28), .Q(e29), .reset(rt));  // open: Qn, preset, en
  and and_4 (and_4_out, e32, e13);
  Multiplexer #(.enable("false")) multiplexer_15 (.in0(in_12), .in1(neg), .out(so3), .sel(s3));
  not not_7 (not_7_out, s4);
  Multiplexer #(.enable("false")) multiplexer_16 (.in0(in_22), .in1(neg), .out(so7), .sel(s7));
  nand nand_3 (fp5, ap3, sp5);
  nand nand_4 (fp4, ap4, sp4);
  D_Flip_Flop d_ff_21 (.clk(rj), .D(e5), .Q(e6), .reset(rt));  // open: Qn, preset, en
  D_Flip_Flop d_ff_22 (.clk(rj), .D(e13), .Q(e14), .reset(rt));  // open: Qn, preset, en
  D_Flip_Flop d_ff_23 (.clk(rj), .D(e21), .Q(e22), .reset(rt));  // open: Qn, preset, en
  D_Flip_Flop d_ff_24 (.clk(rj), .D(e29), .Q(e30), .reset(rt));  // open: Qn, preset, en
  not not_8 (NO, or_30_out);
  or or_30 (or_30_out, undriven, e5, e6, e7, e8, e9, e10, e11, e12, e13, e14, e15, e16, e17, e18);
  Counter #(.ongoal("continue")) counter_1 (.load(rt), .count(and_4_out), .clk(rj));  // open: D, Q, carry, clr
  Multiplexer #(.enable("false")) multiplexer_17 (.in0(in_11), .in1(neg), .out(sp4), .sel(not_7_out));
  D_Flip_Flop d_ff_25 (.clk(rj), .D(e6), .Q(e7), .reset(rt));  // open: Qn, preset, en
  D_Flip_Flop d_ff_26 (.clk(rj), .D(e14), .Q(e15), .reset(rt));  // open: Qn, preset, en
  D_Flip_Flop d_ff_27 (.clk(rj), .D(e22), .Q(e23), .reset(rt));  // open: Qn, preset, en
  D_Flip_Flop d_ff_28 (.clk(rj), .D(e30), .Q(e31), .reset(rt));  // open: Qn, preset, en
  Multiplexer #(.enable("false")) multiplexer_18 (.in0(in_13), .in1(neg), .out(so4), .sel(s4));
  and and_5 (ffp5, sp5, fp5);
  and and_6 (ffp4, sp4, fp4);
  D_Flip_Flop d_ff_29 (.clk(rj), .D(e7), .Q(e8), .reset(rt));  // open: Qn, preset, en
  D_Flip_Flop d_ff_30 (.clk(rj), .D(e15), .Q(e16), .reset(rt));  // open: Qn, preset, en
  D_Flip_Flop d_ff_31 (.clk(rj), .D(e23), .Q(e24), .reset(rt));  // open: Qn, preset, en
  D_Flip_Flop d_ff_32 (.clk(rj), .D(e31), .Q(e32), .reset(rt));  // open: Qn, preset, en
  and and_7 (and_7_out, d, not_9_out);
  not not_9 (not_9_out, A);
  D_Flip_Flop d_ff_33 (.clk(rj), .Q(s), .preset(and_7_out), .reset(e));  // open: D, Qn, en
  Demultiplexer #(.disabled(0), .enable("false")) demultiplexer_1 (.out0(d1a), .out1(d22a), .in(s), .sel(dir));
  D_Flip_Flop d_ff_34 (.clk(rj), .D(or_31_out), .Q(s1));  // open: Qn, preset, en, reset
  or or_31 (or_31_out, d1a, d3b);
  D_Flip_Flop d_ff_35 (.clk(rj), .D(or_32_out), .Q(s2));  // open: Qn, preset, en, reset
  or or_32 (or_32_out, d2a, d4b);
  D_Flip_Flop d_ff_36 (.clk(rj), .D(or_33_out), .Q(s3));  // open: Qn, preset, en, reset
  or or_33 (or_33_out, d3a, d5b);
  D_Flip_Flop d_ff_37 (.clk(rj), .D(or_34_out), .Q(s4));  // open: Qn, preset, en, reset
  or or_34 (or_34_out, d4a, d6b);
  D_Flip_Flop d_ff_38 (.clk(rj), .D(or_35_out), .Q(s5));  // open: Qn, preset, en, reset
  or or_35 (or_35_out, d5a, d7b);
  D_Flip_Flop d_ff_39 (.clk(rj), .D(or_36_out), .Q(s6));  // open: Qn, preset, en, reset
  or or_36 (or_36_out, d6a, d8b);
  D_Flip_Flop d_ff_40 (.clk(rj), .D(or_37_out), .Q(s7));  // open: Qn, preset, en, reset
  or or_37 (or_37_out, d7a, in_4);
  Random #(.width(1)) random_1 (.clk(rj), .out(sa));  // open: next, clr
  Multiplexer #(.enable("false")) multiplexer_19 (.in0(in_14), .in1(1'b1), .out(multiplexer_19_out), .sel(and_8_out));
  Demultiplexer #(.enable("false")) demultiplexer_2 (
    .out0(e1fp), .out1(e1fs), .in(multiplexer_19_out), .sel(and_9_out));
  and and_8 (and_8_out, e1, not_10_out);
  and and_9 (and_9_out, e1, op);
  not not_10 (not_10_out, e20);
  Demultiplexer #(.enable("false")) demultiplexer_3 (
    .out0(e4fp), .out1(e4fs), .in(multiplexer_20_out), .sel(and_10_out));
  Multiplexer #(.enable("false")) multiplexer_20 (.in0(in_23), .in1(1'b1), .out(multiplexer_20_out), .sel(e4));
  and and_10 (and_10_out, e4, op);
  Demultiplexer #(.enable("false")) demultiplexer_4 (
    .out0(e7fp), .out1(e7fs), .in(multiplexer_21_out), .sel(and_11_out));
  Multiplexer #(.enable("false")) multiplexer_21 (.in0(in_27), .in1(1'b1), .out(multiplexer_21_out), .sel(e7));
  and and_11 (and_11_out, e7, op);
  Multiplexer #(.enable("false")) multiplexer_22 (.in0(in_31), .in1(1'b1), .out(multiplexer_22_out), .sel(e10));
  Demultiplexer #(.enable("false")) demultiplexer_5 (
    .out0(e10fp), .out1(e10fs), .in(multiplexer_22_out), .sel(and_12_out));
  and and_12 (and_12_out, e10, op);
  Demultiplexer #(.enable("false")) demultiplexer_6 (
    .out0(e13fp), .out1(e13fs), .in(multiplexer_23_out), .sel(and_13_out));
  Multiplexer #(.enable("false")) multiplexer_23 (.in0(in_34), .in1(1'b1), .out(multiplexer_23_out), .sel(e13));
  and and_13 (and_13_out, e13, op);
  Multiplexer #(.enable("false")) multiplexer_24 (.in0(in_37), .in1(1'b1), .out(multiplexer_24_out), .sel(e16));
  Demultiplexer #(.enable("false")) demultiplexer_7 (
    .out0(e16fp), .out1(e16fs), .in(multiplexer_24_out), .sel(and_14_out));
  and and_14 (and_14_out, e16, op);
  Multiplexer #(.enable("false")) multiplexer_25 (.in0(in_40), .in1(1'b1), .out(multiplexer_25_out), .sel(e19));
  Demultiplexer #(.enable("false")) demultiplexer_8 (
    .out0(e19fp), .out1(e19fs), .in(multiplexer_25_out), .sel(and_15_out));
  and and_15 (and_15_out, e19, op);
  Multiplexer #(.enable("false")) multiplexer_26 (.in0(in_43), .in1(1'b1), .out(multiplexer_26_out), .sel(e22));
  Demultiplexer #(.enable("false")) demultiplexer_9 (
    .out0(e22fp), .out1(e22fs), .in(multiplexer_26_out), .sel(and_16_out));
  and and_16 (and_16_out, e22, op1);
  Multiplexer #(.enable("false")) multiplexer_27 (.in0(in_46), .in1(1'b1), .out(multiplexer_27_out), .sel(e25));
  Demultiplexer #(.enable("false")) demultiplexer_10 (
    .out0(e25fp), .out1(e25fs), .in(multiplexer_27_out), .sel(and_17_out));
  and and_17 (and_17_out, e25, op1);
  Multiplexer #(.enable("false")) multiplexer_28 (.in0(in_49), .in1(1'b1), .out(multiplexer_28_out), .sel(e28));
  Demultiplexer #(.enable("false")) demultiplexer_11 (
    .out0(e28fp), .out1(e28fs), .in(multiplexer_28_out), .sel(and_18_out));
  and and_18 (and_18_out, e28, op1);
  Multiplexer #(.enable("false")) multiplexer_29 (.in0(in_52), .in1(1'b1), .out(multiplexer_29_out), .sel(e31));
  Demultiplexer #(.enable("false")) demultiplexer_12 (
    .out0(e31fp), .out1(e31fs), .in(multiplexer_29_out), .sel(and_19_out));
  and and_19 (and_19_out, e31, op1);
  Demultiplexer #(.disabled(0), .enable("false")) demultiplexer_13 (.out0(d2a), .out1(d2b), .in(s1), .sel(dir));
  Demultiplexer #(.disabled(0), .enable("false")) demultiplexer_14 (.out0(d3a), .out1(d3b), .in(s2), .sel(dir));
  Demultiplexer #(.disabled(0), .enable("false")) demultiplexer_15 (.out0(d4a), .out1(d4b), .in(s3), .sel(dir));
  Demultiplexer #(.disabled(0), .enable("false")) demultiplexer_16 (.out0(d5a), .out1(d5b), .in(s4), .sel(dir));
  Demultiplexer #(.disabled(0), .enable("false")) demultiplexer_17 (.out0(d6a), .out1(d6b), .in(s5), .sel(dir));
  Demultiplexer #(.disabled(0), .enable("false")) demultiplexer_18 (.out0(d7a), .out1(d7b), .in(s6), .sel(dir));
  Demultiplexer #(.disabled(0), .enable("false")) demultiplexer_19 (.out0(d8a), .out1(d8b), .in(s7), .sel(dir));
  D_Flip_Flop d_ff_41 (.clk(rj), .D(sa), .Q(op), .en(obj));  // open: Qn, preset, reset
  D_Flip_Flop d_ff_42 (.clk(rj), .D(op), .Q(op1), .en(e19));  // open: Qn, preset, reset
  Demultiplexer #(.enable("false")) demultiplexer_20 (
    .out0(e2fp), .out1(e2fs), .in(multiplexer_30_out), .sel(and_21_out));
  Multiplexer #(.enable("false")) multiplexer_30 (.in0(in_15), .in1(1'b1), .out(multiplexer_30_out), .sel(and_20_out));
  and and_20 (and_20_out, e2, not_11_out);
  and and_21 (and_21_out, e2, op);
  not not_11 (not_11_out, e21);
  Demultiplexer #(.enable("false")) demultiplexer_21 (
    .out0(e5fp), .out1(e5fs), .in(multiplexer_31_out), .sel(and_22_out));
  Multiplexer #(.enable("false")) multiplexer_31 (.in0(in_24), .in1(1'b1), .out(multiplexer_31_out), .sel(e5));
  and and_22 (and_22_out, e5, op);
  Demultiplexer #(.enable("false")) demultiplexer_22 (
    .out0(e8fp), .out1(e8fs), .in(multiplexer_32_out), .sel(and_23_out));
  Multiplexer #(.enable("false")) multiplexer_32 (.in0(in_28), .in1(1'b1), .out(multiplexer_32_out), .sel(e8));
  and and_23 (and_23_out, e8, op);
  Multiplexer #(.enable("false")) multiplexer_33 (.in0(in_32), .in1(1'b1), .out(multiplexer_33_out), .sel(e11));
  Demultiplexer #(.enable("false")) demultiplexer_23 (
    .out0(e11fp), .out1(e11fs), .in(multiplexer_33_out), .sel(and_24_out));
  and and_24 (and_24_out, e11, op);
  Demultiplexer #(.enable("false")) demultiplexer_24 (
    .out0(e14fp), .out1(e14fs), .in(multiplexer_34_out), .sel(and_25_out));
  Multiplexer #(.enable("false")) multiplexer_34 (.in0(in_35), .in1(1'b1), .out(multiplexer_34_out), .sel(e14));
  and and_25 (and_25_out, e14, op);
  Multiplexer #(.enable("false")) multiplexer_35 (.in0(in_38), .in1(1'b1), .out(multiplexer_35_out), .sel(e17));
  Demultiplexer #(.enable("false")) demultiplexer_25 (
    .out0(e17fp), .out1(e17fs), .in(multiplexer_35_out), .sel(and_26_out));
  and and_26 (and_26_out, e17, op);
  Multiplexer #(.enable("false")) multiplexer_36 (.in0(in_41), .in1(1'b1), .out(multiplexer_36_out), .sel(e20));
  Demultiplexer #(.enable("false")) demultiplexer_26 (
    .out0(e20fp), .out1(e20fs), .in(multiplexer_36_out), .sel(and_27_out));
  and and_27 (and_27_out, e20, op);
  Multiplexer #(.enable("false")) multiplexer_37 (.in0(in_44), .in1(1'b1), .out(multiplexer_37_out), .sel(e23));
  Demultiplexer #(.enable("false")) demultiplexer_27 (
    .out0(e23fp), .out1(e23fs), .in(multiplexer_37_out), .sel(and_28_out));
  and and_28 (and_28_out, e23, op1);
  Demultiplexer #(.enable("false")) demultiplexer_28 (
    .out0(e26fp), .out1(e26fs), .in(multiplexer_38_out), .sel(and_29_out));
  Multiplexer #(.enable("false")) multiplexer_38 (.in0(in_47), .in1(1'b1), .out(multiplexer_38_out), .sel(e26));
  and and_29 (and_29_out, e26, op1);
  Multiplexer #(.enable("false")) multiplexer_39 (.in0(in_50), .in1(1'b1), .out(multiplexer_39_out), .sel(e29));
  Demultiplexer #(.enable("false")) demultiplexer_29 (
    .out0(e29fp), .out1(e29fs), .in(multiplexer_39_out), .sel(and_30_out));
  and and_30 (and_30_out, e29, op1);
  Demultiplexer #(.enable("false")) demultiplexer_30 (
    .out0(e32fp), .out1(e32fs), .in(multiplexer_40_out), .sel(and_31_out));
  Multiplexer #(.enable("false")) multiplexer_40 (.in0(in_53), .in1(1'b1), .out(multiplexer_40_out), .sel(e32));
  and and_31 (and_31_out, e32, op1);
  not not_12 (prn, obj);
  not not_13 (neg, in_2);
  Comparator #(.width(1)) comparator_4 (.a(d2b), .b(s1), .lt(e));  // open: gt, eq
  T_Flip_Flop t_ff_1 (.Q(dir), .preset(s7), .reset(e));  // open: clk, T, Qn, en
  and and_32 (and_32_out, a_t, not_14_out);
  not not_14 (not_14_out, s);
  Demultiplexer #(.enable("false")) demultiplexer_31 (
    .out0(e3fp), .out1(e3fs), .in(multiplexer_41_out), .sel(and_33_out));
  Multiplexer #(.enable("false")) multiplexer_41 (.in0(in_16), .in1(1'b1), .out(multiplexer_41_out), .sel(e3));
  and and_33 (and_33_out, e3, op);
  Demultiplexer #(.enable("false")) demultiplexer_32 (
    .out0(e6fp), .out1(e6fs), .in(multiplexer_42_out), .sel(and_34_out));
  Multiplexer #(.enable("false")) multiplexer_42 (.in0(in_25), .in1(1'b1), .out(multiplexer_42_out), .sel(e6));
  and and_34 (and_34_out, e6, op);
  Multiplexer #(.enable("false")) multiplexer_43 (.in0(in_29), .in1(1'b1), .out(multiplexer_43_out), .sel(e9));
  Demultiplexer #(.enable("false")) demultiplexer_33 (
    .out0(e9fp), .out1(e9fs), .in(multiplexer_43_out), .sel(and_35_out));
  and and_35 (and_35_out, e9, op);
  Multiplexer #(.enable("false")) multiplexer_44 (.in0(in_33), .in1(1'b1), .out(multiplexer_44_out), .sel(e12));
  Demultiplexer #(.enable("false")) demultiplexer_34 (
    .out0(e12fp), .out1(e12fs), .in(multiplexer_44_out), .sel(and_36_out));
  and and_36 (and_36_out, e12, op);
  Demultiplexer #(.enable("false")) demultiplexer_35 (
    .out0(e15fp), .out1(e15fs), .in(multiplexer_45_out), .sel(and_37_out));
  Multiplexer #(.enable("false")) multiplexer_45 (.in0(in_36), .in1(1'b1), .out(multiplexer_45_out), .sel(e15));
  and and_37 (and_37_out, e15, op);
  Multiplexer #(.enable("false")) multiplexer_46 (.in0(in_39), .in1(1'b1), .out(multiplexer_46_out), .sel(e18));
  Demultiplexer #(.enable("false")) demultiplexer_36 (
    .out0(e18fp), .out1(e18fs), .in(multiplexer_46_out), .sel(and_38_out));
  and and_38 (and_38_out, e18, op);
  Demultiplexer #(.enable("false")) demultiplexer_37 (
    .out0(e21fp), .out1(e21fs), .in(multiplexer_47_out), .sel(and_39_out));
  Multiplexer #(.enable("false")) multiplexer_47 (.in0(in_42), .in1(1'b1), .out(multiplexer_47_out), .sel(e21));
  and and_39 (and_39_out, e21, op1);
  Demultiplexer #(.enable("false")) demultiplexer_38 (
    .out0(e24fp), .out1(e24fs), .in(multiplexer_48_out), .sel(and_40_out));
  Multiplexer #(.enable("false")) multiplexer_48 (.in0(in_45), .in1(1'b1), .out(multiplexer_48_out), .sel(e24));
  and and_40 (and_40_out, e24, op1);
  Multiplexer #(.enable("false")) multiplexer_49 (.in0(in_48), .in1(1'b1), .out(multiplexer_49_out), .sel(e27));
  Demultiplexer #(.enable("false")) demultiplexer_39 (
    .out0(e27fp), .out1(e27fs), .in(multiplexer_49_out), .sel(and_41_out));
  and and_41 (and_41_out, e27, op1);
  Multiplexer #(.enable("false")) multiplexer_50 (.in0(in_51), .in1(1'b1), .out(multiplexer_50_out), .sel(e30));
  Demultiplexer #(.enable("false")) demultiplexer_40 (
    .out0(e30fp), .out1(e30fs), .in(multiplexer_50_out), .sel(and_42_out));
  and and_42 (and_42_out, e30, op1);
  D_Flip_Flop d_ff_43 (.clk(rj), .Q(A), .preset(and_32_out), .reset(f));  // open: D, Qn, en
  Demultiplexer #(.disabled(0), .enable("false")) demultiplexer_41 (.out0(a1a), .in(A), .sel(dirs));  // open: out1
  or or_38 (or_38_out, a1a, a3b);
  or or_39 (or_39_out, a2a, a4b);
  or or_40 (or_40_out, a3a, a5b);
  or or_41 (or_41_out, a4a, in_5);
  D_Flip_Flop d_ff_44 (.clk(rj), .D(or_38_out), .Q(a1));  // open: Qn, preset, en, reset
  Demultiplexer #(.disabled(0), .enable("false")) demultiplexer_42 (.out0(a2a), .out1(a2b), .in(a1), .sel(dirs));
  Demultiplexer #(.disabled(0), .enable("false")) demultiplexer_43 (.out0(a3a), .out1(a3b), .in(a2), .sel(dirs));
  D_Flip_Flop d_ff_45 (.clk(rj), .D(or_39_out), .Q(a2));  // open: Qn, preset, en, reset
  Demultiplexer #(.disabled(0), .enable("false")) demultiplexer_44 (.out0(a4a), .out1(a4b), .in(a3), .sel(dirs));
  D_Flip_Flop d_ff_46 (.clk(rj), .D(or_40_out), .Q(a3));  // open: Qn, preset, en, reset
  Demultiplexer #(.disabled(0), .enable("false")) demultiplexer_45 (.out0(a5a), .out1(a5b), .in(a4), .sel(dirs));
  D_Flip_Flop d_ff_47 (.clk(rj), .D(or_41_out), .Q(a4));  // open: Qn, preset, en, reset
  and and_43 (and_43_out, ffp4, e31fp);
  and and_44 (and_44_out, ffp5, e30fp);
  and and_45 (and_45_out, ffp7, e30fs);
  and and_46 (and_46_out, ffp7, e31fs);
  and and_47 (and_47_out, so1, e30fs);
  and and_48 (and_48_out, so1, e31fs);
  and and_49 (and_49_out, so2, e30fs);
  and and_50 (and_50_out, so2, e31fs);
  and and_51 (and_51_out, so3, e31fs);
  and and_52 (and_52_out, so3, e30fs);
  and and_53 (and_53_out, so4, e30fs);
  and and_54 (and_54_out, so4, e31fs);
  and and_55 (and_55_out, so5, e31fs);
  and and_56 (and_56_out, so5, e30fs);
  and and_57 (and_57_out, so6, e30fs);
  and and_58 (and_58_out, so6, e31fs);
  and and_59 (and_59_out, so7, e31fs);
  and and_60 (and_60_out, so7, e30fs);
  and and_61 (and_61_out, sp2, e31fp);
  and and_62 (and_62_out, sp3, e30fp);
  and and_63 (and_63_out, sp3, e31fp);
  and and_64 (and_64_out, ffp4, e30fp);
  Comparator #(.width(1)) comparator_5 (.a(a2b), .b(a1), .lt(f));  // open: gt, eq
  T_Flip_Flop t_ff_2 (.Q(dirs), .preset(a4), .reset(f));  // open: clk, T, Qn, en
  and and_65 (and_65_out, sp1, e30fp);
  and and_66 (and_66_out, sp1, e31fp);
  and and_67 (and_67_out, sp2, e30fp);
  or or_42 (or_42_out, and_65_out, and_66_out, and_67_out, and_61_out, and_62_out, and_63_out, and_64_out, and_43_out, and_44_out, and_45_out, and_46_out, and_47_out, and_48_out, and_49_out, and_50_out, and_51_out, and_52_out, and_53_out, and_54_out, and_55_out, and_56_out, and_57_out, and_58_out, and_59_out, and_60_out);
  Clock clock_1 (.out(clock_1_out));
  and and_68 (rj, clock_1_out, not_15_out);
  not not_15 (not_15_out, or_42_out);

  // Other names for the same wires on the sheet: t1[31:0] = {e32fp, _31f1, _30f1, e29fp, e28fp, e27fp, e26fp, e25fp, e24fp, e23fp, e22fp, e21fp, e20fp, e19fp, e18fp, e17fp, e16fp, e15fp, e14fp, e13fp, e12fp, e11fp, e10fp, e9fp, e8fp, e7fp, e6fp, e5fp, e4fp, e3fp, e2fp, e1fp};
  //   t2[31:0] = {e32fp, _31f2, _30f2, e29fp, e28fp, e27fp, e26fp, e25fp, e24fp, e23fp, e22fp, e21fp, e20fp, e19fp, e18fp, e17fp, e16fp, e15fp, e14fp, e13fp, e12fp, e11fp, e10fp, e9fp, e8fp, e7fp, e6fp, e5fp, e4fp, e3fp, e2fp, e1fp};
  //   t3[31:0] = {e32fp, _31f3, _30f3, e29fp, e28fp, e27fp, e26fp, e25fp, e24fp, e23fp, e22fp, e21fp, e20fp, e19fp, e18fp, e17fp, e16fp, e15fp, e14fp, e13fp, e12fp, e11fp, e10fp, e9fp, e8fp, e7fp, e6fp, e5fp, e4fp, e3fp, e2fp, e1fp};
  //   t4[31:0] = {e32fp, _31f4, _30f4, e29fp, e28fp, e27fp, e26fp, e25fp, e24fp, e23fp, e22fp, e21fp, e20fp, e19fp, e18fp, e17fp, e16fp, e15fp, e14fp, e13fp, e12fp, e11fp, e10fp, e9fp, e8fp, e7fp, e6fp, e5fp, e4fp, e3fp, e2fp, e1fp};
  //   t5[31:0] = {e32fp, _31f5, _30f5, e29fp, e28fp, e27fp, e26fp, e25fp, e24fp, e23fp, e22fp, e21fp, e20fp, e19fp, e18fp, e17fp, e16fp, e15fp, e14fp, e13fp, e12fp, e11fp, e10fp, e9fp, e8fp, e7fp, e6fp, e5fp, e4fp, e3fp, e2fp, e1fp};
  //   t6[31:0] = {in_3, _31f6, _30f6, {29{in_1}}};
  //   t7[31:0] = {e32fs, _31f7, _30f7, e29fs, e28fs, e27fs, e26fs, e25fs, e24fs, e23fs, e22fs, e21fs, e20fs, e19fs, e18fs, e17fs, e16fs, e15fs, e14fs, e13fs, e12fs, e11fs, e10fs, e9fs, e8fs, e7fs, e6fs, e5fs, e4fs, e3fs, e2fs, e1fs};
  //   t8[31:0] = {e32fs, _31f8, _30f8, e29fs, e28fs, e27fs, e26fs, e25fs, e24fs, e23fs, e22fs, e21fs, e20fs, e19fs, e18fs, e17fs, e16fs, e15fs, e14fs, e13fs, e12fs, e11fs, e10fs, e9fs, e8fs, e7fs, e6fs, e5fs, e4fs, e3fs, e2fs, e1fs};
  //   t9[31:0] = {e32fs, _31f9, _30f9, e29fs, e28fs, e27fs, e26fs, e25fs, e24fs, e23fs, e22fs, e21fs, e20fs, e19fs, e18fs, e17fs, e16fs, e15fs, e14fs, e13fs, e12fs, e11fs, e10fs, e9fs, e8fs, e7fs, e6fs, e5fs, e4fs, e3fs, e2fs, e1fs};
  //   t10[31:0] = {e32fs, _31f10, _30f10, e29fs, e28fs, e27fs, e26fs, e25fs, e24fs, e23fs, e22fs, e21fs, e20fs, e19fs, e18fs, e17fs, e16fs, e15fs, e14fs, e13fs, e12fs, e11fs, e10fs, e9fs, e8fs, e7fs, e6fs, e5fs, e4fs, e3fs, e2fs, e1fs};
  //   t11[31:0] = {e32fs, _31f11, _30f11, e29fs, e28fs, e27fs, e26fs, e25fs, e24fs, e23fs, e22fs, e21fs, e20fs, e19fs, e18fs, e17fs, e16fs, e15fs, e14fs, e13fs, e12fs, e11fs, e10fs, e9fs, e8fs, e7fs, e6fs, e5fs, e4fs, e3fs, e2fs, e1fs};
  //   t12[31:0] = {e32fs, _31f12, _30f12, e29fs, e28fs, e27fs, e26fs, e25fs, e24fs, e23fs, e22fs, e21fs, e20fs, e19fs, e18fs, e17fs, e16fs, e15fs, e14fs, e13fs, e12fs, e11fs, e10fs, e9fs, e8fs, e7fs, e6fs, e5fs, e4fs, e3fs, e2fs, e1fs};
  //   t13[31:0] = {e32fs, _31f13, _30f13, e29fs, e28fs, e27fs, e26fs, e25fs, e24fs, e23fs, e22fs, e21fs, e20fs, e19fs, e18fs, e17fs, e16fs, e15fs, e14fs, e13fs, e12fs, e11fs, e10fs, e9fs, e8fs, e7fs, e6fs, e5fs, e4fs, e3fs, e2fs, e1fs};
  //   t14[31:0] = {e32fs, _31f14, _30f14, e29fs, e28fs, e27fs, e26fs, e25fs, e24fs, e23fs, e22fs, e21fs, e20fs, e19fs, e18fs, e17fs, e16fs, e15fs, e14fs, e13fs, e12fs, e11fs, e10fs, e9fs, e8fs, e7fs, e6fs, e5fs, e4fs, e3fs, e2fs, e1fs};
  //   t15[31:0] = {e32fs, e31fs, e30fs, e29fs, e28fs, e27fs, e26fs, e25fs, e24fs, e23fs, e22fs, e21fs, e20fs, e19fs, e18fs, e17fs, e16fs, e15fs, e14fs, e13fs, e12fs, e11fs, e10fs, e9fs, e8fs, e7fs, e6fs, e5fs, e4fs, e3fs, e2fs, e1fs};
  //   t16[31:0] = {e32fs, e31fs, e30fs, e29fs, e28fs, e27fs, e26fs, e25fs, e24fs, e23fs, e22fs, e21fs, e20fs, e19fs, e18fs, e17fs, e16fs, e15fs, e14fs, e13fs, e12fs, e11fs, e10fs, e9fs, e8fs, e7fs, e6fs, e5fs, e4fs, e3fs, e2fs, e1fs}

  // Notes on the sheet:
  //   PRESIONE PARA JUGAR
  //   'w': SALTAR
  //   'v': EMPEZAR
  //   PUNTAJE
  //   'y': AGACHARSE
  //   RESETEAR
  //   CON SO1 PRENDO 30f8  y 31f8
  //   Saltar
  //   ALEATORIO
  //   fp:abajo
  //   fs:arriba
  //   Agacharse
endmodule
