// Logisim project proyectoObstaculo.circ as structural Verilog: 1 circuit, main circuit main
module main (
  input  in_1,
  input  in_2,
  input  in_3,
  input  in_4,
  input  in_5,
  input  in_6,
  input  in_7,
  input  in_8,
  input  in_9,
  input  in_10,
  input  in_11
);

  wire ag, button_1_out, button_2_out, e1, e2, e3, e4, jp, not_4_out, not_6_out, rj;
  wire [0:0] t1, t2, t3, t4;

  Clock clock_1 (.out(rj));
  not not_1 (t1[0], in_5);
  D_Flip_Flop d_ff_1 (.clk(rj), .D(e4), .Q(e1));  // open: Qn, preset, en, reset
  D_Flip_Flop d_ff_2 (.clk(rj), .D(e3), .Q(e4));  // open: Qn, preset, en, reset
  not not_2 (t2[0], in_6);
  D_Flip_Flop d_ff_3 (.clk(rj), .D(e1), .Q(e2));  // open: Qn, preset, en, reset
  DotMatrix #(.matrixcols(4), .matrixrows(3)) dotmatrix_1 (
    .col0({ag, jp, t1[0]}), .col1({in_11, e4, t4[0]}), .col2({in_10, e3, t3[0]}), .col3({in_9, e2, t2[0]}));
  D_Flip_Flop d_ff_4 (.clk(rj), .D(e2), .Q(e3));  // open: Qn, preset, en, reset
  not not_3 (t3[0], in_7);
  not not_4 (not_4_out, in_3);
  Button button_1 (.out(button_1_out));
  not not_5 (t4[0], in_8);
  not not_6 (not_6_out, in_1);
  Multiplexer #(.enable("false")) multiplexer_1 (.in0(not_4_out), .in1(in_4), .out(jp), .sel(button_1_out));
  Multiplexer #(.enable("false")) multiplexer_2 (.in0(not_6_out), .in1(in_2), .out(ag), .sel(button_2_out));
  Button button_2 (.out(button_2_out));

  // Other names for the same wires on the sheet: t1[2:1] = {ag, jp}; t2[2:1] = {in_9, e2}; t3[2:1] = {in_10, e3};
  //   t4[2:1] = {in_11, e4}

  // Notes on the sheet:
  //   if e1 and 2 : restart
  //   saltar
  //   agacharse
endmodule
